# Fritzing sketch external_power_supply (saved by Fritzing 0.9.3b)
breadboards: 1

parts:
  Part1 = Arduino Uno (Rev3) - ICSP
  KY-1 = KY-037 Sound Sensor Module [package="Breakout board"]
  TD-er1 = MH-Z19 CO2 sensor [part_number=MH-Z19]

nets:
  N1: Part1.A0, KY-1.A0
  N2: Part1.D4, TD-er1.PWM
  N3: Part1.5V, KY-1.+
  GND: Part1.GND, KY-1.G, TD-er1.GND

notes:
  Goes to 5V external power supply.
  Needs to be connected with Arduino GND!

custom parts:
  KY-037 Sound Sensor Module: Microphone Sound Sensor. It reacts on specific sound volume (Digital Output).
